// Logisim project TerrAltair.circ as structural Verilog: 8 circuits, main circuit main
module main (
  input  [9:0] in_1,
  input  input_number
);

  wire alu_fullmodule_1_out_6, alu_fullmodule_1_out_8, alu_fullmodule_1_out_9, and_1_out, and_2_out,
       and_3_out, clock_1_out, cpu_clock_out, decoder_1_out0, decoder_1_out1, decoder_1_out2, decoder_1_out3,
       demultiplexer_1_out0, demultiplexer_1_out1, demultiplexer_1_out2, demultiplexer_1_out3,
       demultiplexer_1_out4, demultiplexer_1_out5, demultiplexer_1_out6, demultiplexer_1_out7,
       input_confirm_out, io_fullmodule_1_out_15, io_fullmodule_1_out_25, io_fullmodule_1_out_26,
       io_fullmodule_1_out_27, io_fullmodule_1_out_28, io_fullmodule_1_out_33, io_fullmodule_1_out_34,
       io_fullmodule_1_out_35, io_fullmodule_1_out_36, not_1_out, not_2_out, or_1_out, or_2_out, or_3_out,
       or_4_out, or_5_out, or_6_out, reset_out, ttcpu_inputator_1_out_7;
  wire [2:0] cpu_rom_data_3;
  wire [9:0] A_q, adder_1_out, B_q, cpu_rom_data, demultiplexer_2_out0, demultiplexer_2_out1,
       demultiplexer_2_out2, demultiplexer_3_out0, demultiplexer_3_out1, demultiplexer_3_out2,
       demultiplexer_3_out3, io_fullmodule_1_out_16, io_fullmodule_1_out_17, io_fullmodule_1_out_18,
       io_fullmodule_1_out_19, io_fullmodule_1_out_24, J_q, M_q, multiplexer_1_out, multiplexer_2_out,
       multiplexer_3_out, multiplexer_4_out, multiplexer_5_out, multiplexer_6_out, multiplexer_7_out, PRC_q,
       pull_resistor_1_node, ram_1_dout, S_q, subtractor_1_out, subtractor_2_out, ttcpu_7seg_1_out_5,
       ttcpu_7seg_2_out_5, ttcpu_7seg_3_out_5, ttcpu_inputator_1_out_8, X_q, Y_q;
  wire [9:1] pull_resistor_2_node;
  wire [19:10] cpu_rom_data_2;

  TTcpu_7seg ttcpu_7seg_1 (
    .in_4(or_3_out), .in_1(io_fullmodule_1_out_16), .in_2(io_fullmodule_1_out_25),
    .in_3(io_fullmodule_1_out_33), .out_5(ttcpu_7seg_1_out_5));
  TTcpu_7seg ttcpu_7seg_2 (
    .in_4(or_3_out), .in_1(io_fullmodule_1_out_17), .in_2(io_fullmodule_1_out_26),
    .in_3(io_fullmodule_1_out_34), .out_5(ttcpu_7seg_2_out_5));
  TTcpu_7seg ttcpu_7seg_3 (
    .in_4(or_3_out), .in_1(io_fullmodule_1_out_18), .in_2(io_fullmodule_1_out_27),
    .in_3(io_fullmodule_1_out_35), .out_5(ttcpu_7seg_3_out_5));
  Button input_confirm (.out(input_confirm_out));
  or or_1 (or_1_out, input_confirm_out, input_number);
  TTcpu_display ttcpu_display_1 ();  // open: in_1, in_2, in_3, in_4, in_5
  TTcpu_inputator ttcpu_inputator_1 (
    .in_1(in_1), .in_6(or_3_out), .in_2(io_fullmodule_1_out_19), .in_3(io_fullmodule_1_out_28),
    .in_4(io_fullmodule_1_out_36), .in_5(or_1_out), .out_7(ttcpu_inputator_1_out_7),
    .out_8(ttcpu_inputator_1_out_8));
  LED led_1 (.in(ttcpu_inputator_1_out_7));
  Clock clock_1 (.out(clock_1_out));
  or or_2 (or_2_out, clock_1_out, cpu_clock_out);
  Button cpu_clock (.out(cpu_clock_out));
  Button reset (.out(reset_out));
  io_fullmodule io_fullmodule_1 (
    .in_13(and_2_out), .in_14(or_3_out), .in_11(demultiplexer_2_out2), .in_1(decoder_1_out2),
    .in_12(demultiplexer_3_out2), .in_6(multiplexer_4_out), .in_2(ttcpu_7seg_1_out_5),
    .in_3(ttcpu_7seg_2_out_5), .in_4(ttcpu_7seg_3_out_5), .in_5(ttcpu_inputator_1_out_8),
    .out_15(io_fullmodule_1_out_15), .out_24(io_fullmodule_1_out_24), .out_16(io_fullmodule_1_out_16),
    .out_17(io_fullmodule_1_out_17), .out_18(io_fullmodule_1_out_18), .out_19(io_fullmodule_1_out_19),
    .out_25(io_fullmodule_1_out_25), .out_26(io_fullmodule_1_out_26), .out_27(io_fullmodule_1_out_27),
    .out_28(io_fullmodule_1_out_28), .out_33(io_fullmodule_1_out_33), .out_34(io_fullmodule_1_out_34),
    .out_35(io_fullmodule_1_out_35), .out_36(io_fullmodule_1_out_36));  // open: in_7, in_8, in_9, in_10, out_20, out_21, out_22, out_23, out_29, out_30, out_31, out_32, out_37, out_38, out_39, out_40
  and and_1 (and_1_out, demultiplexer_3_out3[0], decoder_1_out3);
  not not_1 (not_1_out, and_1_out);
  and and_2 (and_2_out, or_2_out, not_1_out);
  or or_3 (or_3_out, reset_out, demultiplexer_3_out3[1]);
  Register #(.width(10)) A (
    .D(io_fullmodule_1_out_24), .en(demultiplexer_1_out0), .Q(A_q), .clk(and_2_out), .clr(or_3_out));
  Register #(.width(10)) B (
    .D(io_fullmodule_1_out_24), .en(demultiplexer_1_out1), .Q(B_q), .clk(and_2_out), .clr(or_3_out));
  Register #(.width(10)) M (
    .D(io_fullmodule_1_out_24), .en(demultiplexer_1_out2), .Q(M_q), .clk(and_2_out), .clr(or_3_out));
  Multiplexer #(.width(10)) multiplexer_1 (
    .in0(M_q), .in1(subtractor_1_out), .out(multiplexer_1_out), .sel(demultiplexer_3_out0[1]));
  RAM #(.addrWidth(10), .asyncread("true"), .dataWidth(10)) ram_1 (
    .addr(multiplexer_1_out), .we(demultiplexer_1_out3), .clk(and_2_out), .din(io_fullmodule_1_out_24),
    .dout(ram_1_dout));  // open: oe
  Multiplexer #(.width(10)) multiplexer_2 (
    .in0(J_q), .in1(cpu_rom_data), .out(multiplexer_2_out), .sel(alu_fullmodule_1_out_8));
  ROM #(.addrWidth(10), .dataWidth(20)) cpu_rom (
    .addr(PRC_q), .data({cpu_rom_data_2[19:18], cpu_rom_data_3, cpu_rom_data_2[14:10], cpu_rom_data}));
  Counter #(.max('h3ff), .width(10)) PRC (
    .load(alu_fullmodule_1_out_9), .D(multiplexer_2_out), .Q(PRC_q), .clk(and_2_out), .clr(or_3_out));  // open: count, carry, up
  or or_4 (or_4_out, decoder_1_out0, not_2_out);
  Demultiplexer #(.select(3)) demultiplexer_1 (
    .out0(demultiplexer_1_out0), .out1(demultiplexer_1_out1), .out2(demultiplexer_1_out2),
    .out3(demultiplexer_1_out3), .out4(demultiplexer_1_out4), .out5(demultiplexer_1_out5),
    .out6(demultiplexer_1_out6), .out7(demultiplexer_1_out7), .in(or_4_out), .sel(cpu_rom_data_3));
  Register #(.width(10)) X (
    .D(io_fullmodule_1_out_24), .en(demultiplexer_1_out4), .Q(X_q), .clk(and_2_out), .clr(or_3_out));
  Register #(.width(10)) Y (
    .D(io_fullmodule_1_out_24), .en(demultiplexer_1_out5), .Q(Y_q), .clk(and_2_out), .clr(or_3_out));
  Register #(.width(10)) S (.D(multiplexer_3_out), .en(or_5_out), .Q(S_q), .clk(and_2_out), .clr(or_3_out));
  or or_5 (or_5_out, demultiplexer_1_out6, demultiplexer_3_out0[1]);
  Register #(.width(10)) J (
    .D(io_fullmodule_1_out_24), .en(demultiplexer_1_out7), .Q(J_q), .clk(and_2_out), .clr(or_3_out));
  Multiplexer #(.width(10)) multiplexer_3 (
    .in0(io_fullmodule_1_out_24), .in1(multiplexer_6_out), .out(multiplexer_3_out),
    .sel(demultiplexer_3_out0[1]));
  not not_2 (not_2_out, or_6_out);
  or or_6 (or_6_out, decoder_1_out3, and_3_out, alu_fullmodule_1_out_6);
  Subtractor #(.width(10)) subtractor_1 (.a(S_q), .b(pull_resistor_1_node), .out(subtractor_1_out));  // open: bin, bout
  Pull_Resistor pull_resistor_1 (.node(pull_resistor_1_node));
  and and_3 (and_3_out, decoder_1_out2, io_fullmodule_1_out_15);
  Multiplexer #(.select(3), .width(10)) multiplexer_4 (
    .in0(A_q), .in1(B_q), .in2(M_q), .in3(ram_1_dout), .in4(X_q), .in5(Y_q), .in6(S_q), .in7(J_q),
    .out(multiplexer_4_out), .sel(cpu_rom_data_3));
  Pull_Resistor pull_resistor_2 (.node({pull_resistor_2_node, demultiplexer_3_out0[1]}));
  Demultiplexer #(.select(2), .width(10)) demultiplexer_2 (
    .out0(demultiplexer_2_out0), .out1(demultiplexer_2_out1), .out2(demultiplexer_2_out2), .in(cpu_rom_data),
    .sel(cpu_rom_data_2[19:18]));  // open: out3
  Demultiplexer #(.select(2), .width(10)) demultiplexer_3 (
    .out0(demultiplexer_3_out0), .out1(demultiplexer_3_out1), .out2(demultiplexer_3_out2),
    .out3(demultiplexer_3_out3), .in({cpu_rom_data_2[19:18], cpu_rom_data_3, cpu_rom_data_2[14:10]}),
    .sel(cpu_rom_data_2[19:18]));
  // Probe on {cpu_rom_data_2[19:18], cpu_rom_data_3, cpu_rom_data_2[14:10]}
  // Probe on cpu_rom_data
  Multiplexer #(.select(3), .width(10)) multiplexer_5 (
    .in0(A_q), .in1(B_q), .in2(M_q), .in3(ram_1_dout), .in4(X_q), .in5(Y_q), .in6(S_q), .in7(J_q),
    .out(multiplexer_5_out), .sel(cpu_rom_data_2[14:12]));
  Comparator #(.mode("unsigned"), .width(3)) comparator_1 (
    .a(cpu_rom_data_2[14:12]), .b(3'b011), .eq(pull_resistor_1_node[0]));  // open: gt, lt
  Subtractor #(.width(10)) subtractor_2 (
    .a(S_q), .b({pull_resistor_2_node, demultiplexer_3_out0[1]}), .out(subtractor_2_out));  // open: bin, bout
  Adder #(.width(10)) adder_1 (
    .a(S_q), .b({pull_resistor_2_node, demultiplexer_3_out0[1]}), .out(adder_1_out));  // open: cin, cout
  Multiplexer #(.width(10)) multiplexer_6 (
    .in0(adder_1_out), .in1(subtractor_2_out), .out(multiplexer_6_out), .sel(pull_resistor_1_node[0]));
  Decoder #(.enable("false"), .select(2)) decoder_1 (
    .out0(decoder_1_out0), .out1(decoder_1_out1), .out2(decoder_1_out2), .out3(decoder_1_out3),
    .sel(cpu_rom_data_2[19:18]));
  assign io_fullmodule_1_out_24 = decoder_1_out0 ? multiplexer_7_out : 10'bz;  // Controlled_Buffer controlled_buffer_1
  Multiplexer #(.width(10)) multiplexer_7 (
    .in0(multiplexer_5_out), .in1(demultiplexer_2_out0), .out(multiplexer_7_out),
    .sel(demultiplexer_3_out0[0]));
  ALU_fullmodule alu_fullmodule_1 (
    .in_1(multiplexer_4_out), .in_3(multiplexer_5_out), .out_7(io_fullmodule_1_out_24),
    .out_6(alu_fullmodule_1_out_6), .out_8(alu_fullmodule_1_out_8), .out_9(alu_fullmodule_1_out_9),
    .in_2(decoder_1_out1), .in_4(demultiplexer_3_out1), .in_5(demultiplexer_2_out1));

  // Notes on the sheet:
  //   contents of cpu_rom (hex, n*v repeats v):
  //   18c02 41c0d 23800 a6000 18c06 41c0d 2b800 ae400 65000 a6800 18c0c 41c0d c0800 3840e 86d01 82c00
  //   86d00 40420 3b800 82c00 18800 40c20
endmodule

module ALU (
  input  [9:0] in_1,
  input  [9:0] in_2,
  input  [3:0] in_3,
  output [9:0] out_4,
  output [9:0] out_5
);

  wire [9:0] adder_1_out, and_1_out, divider_1_out, multiplier_1_out, multiplier_2_out, not_1_out, or_1_out,
       shifter_1_out, shifter_2_out, subtractor_1_out, subtractor_2_out, xor_1_out;

  Adder #(.width(10)) adder_1 (.a(in_1), .b(in_2), .out(adder_1_out), .cout(out_4[3]));  // open: cin
  Subtractor #(.width(10)) subtractor_1 (.a(in_1), .b(in_2), .out(subtractor_1_out), .bout(out_4[0]));  // open: bin
  Shifter #(.width(10)) shifter_1 (.in(in_1), .\dist (in_2[3:0]), .out(shifter_1_out));
  Shifter #(.shift("lr"), .width(10)) shifter_2 (.in(in_1), .\dist (in_2[3:0]), .out(shifter_2_out));
  Multiplier #(.width(10)) multiplier_1 (.a(in_1), .b(in_2), .out(multiplier_1_out));  // open: cin, cout
  Divider #(.width(10)) divider_1 (.a(in_1), .b(in_2), .out(divider_1_out));  // open: upper, rem
  Multiplier #(.width(10)) multiplier_2 (.a(divider_1_out), .b(in_2), .out(multiplier_2_out));  // open: cin, cout
  assign not_1_out = ~in_1;  // NOT_Gate not_1, 10 bits wide
  assign and_1_out = in_1 & in_2;  // AND_Gate and_1, 10 bits wide
  assign or_1_out = in_1 | in_2;  // OR_Gate or_1, 10 bits wide
  Subtractor #(.width(10)) subtractor_2 (.a(in_1), .b(multiplier_2_out), .out(subtractor_2_out));  // open: bin, bout
  assign xor_1_out = in_1 ^ in_2;  // XOR_Gate xor_1, 10 bits wide
  Comparator #(.mode("unsigned"), .width(10)) comparator_1 (.a(out_5), .b({10{1'b0}}), .eq(out_4[2]));  // open: gt, lt
  Multiplexer #(.select(4), .width(10)) multiplexer_1 (
    .in0(adder_1_out), .in1(subtractor_1_out), .in2(shifter_1_out), .in3(shifter_2_out),
    .in4(multiplier_1_out), .in5(divider_1_out), .in6(subtractor_2_out), .in7({{6{1'b0}}, out_4[3:0]}),
    .in8(not_1_out), .in9(and_1_out), .in10(or_1_out), .in11(xor_1_out), .in12({10{1'b0}}),
    .in13({10{1'b0}}), .in14({10{1'b0}}), .in15({10{1'b0}}), .out(out_5), .sel(in_3));
  not not_2 (out_4[1], out_5[0]);

  assign out_4[9:4] = {6{1'b0}};
endmodule

module ALU_fullmodule (
  input  [9:0] in_1,
  input  in_2,
  input  [9:0] in_3,
  input  [9:0] in_4,
  input  [9:0] in_5,
  output out_6,
  output [9:0] out_7,
  output out_8,
  output out_9
);

  wire and_2_out, comparator_1_eq, or_2_out, xnor_1_out;
  wire [9:0] alu_1_out_4, alu_1_out_5, multiplexer_1_out;
  wire [9:5] pull_resistor_1_node;

  Multiplexer #(.width(10)) multiplexer_1 (
    .in0(in_3), .in1({pull_resistor_1_node, in_5[4:0]}), .out(multiplexer_1_out), .sel(in_5[5]));
  assign out_7 = in_2 ? alu_1_out_5 : 10'bz;  // Controlled_Buffer controlled_buffer_1
  ALU alu_1 (.in_1(in_1), .in_2(multiplexer_1_out), .out_4(alu_1_out_4), .in_3(in_5[9:6]), .out_5(alu_1_out_5));
  Pull_Resistor pull_resistor_1 (.node({pull_resistor_1_node, in_5[4:0]}));
  or or_1 (out_6, in_4[0], in_4[1]);
  Comparator #(.width(2)) comparator_1 (.a(in_4[1:0]), .b(2'b11), .eq(comparator_1_eq));  // open: gt, lt
  and and_1 (out_8, in_4[2], comparator_1_eq);
  xnor xnor_1 (xnor_1_out, alu_1_out_4[2], in_4[0]);
  and and_2 (and_2_out, out_6, xnor_1_out);
  or or_2 (or_2_out, comparator_1_eq, and_2_out);
  and and_3 (out_9, or_2_out, in_2);
endmodule

module io_fullmodule (
  input  in_1,
  input  [9:0] in_2,
  input  [9:0] in_3,
  input  [9:0] in_4,
  input  [9:0] in_5,
  input  [9:0] in_6,
  input  [9:0] in_7,
  input  [9:0] in_8,
  input  [9:0] in_9,
  input  [9:0] in_10,
  input  [9:0] in_11,
  input  [9:0] in_12,
  input  in_13,
  input  in_14,
  output out_15,
  output [9:0] out_16,
  output [9:0] out_17,
  output [9:0] out_18,
  output [9:0] out_19,
  output [9:0] out_20,
  output [9:0] out_21,
  output [9:0] out_22,
  output [9:0] out_23,
  output [9:0] out_24,
  output out_25,
  output out_26,
  output out_27,
  output out_28,
  output out_29,
  output out_30,
  output out_31,
  output out_32,
  output out_33,
  output out_34,
  output out_35,
  output out_36,
  output out_37,
  output out_38,
  output out_39,
  output out_40
);

  wire and_1_out, and_2_out, buffer_1_out, buffer_2_out, not_1_out;
  wire [2:0] register_1_q;
  wire [9:0] multiplexer_1_out, multiplexer_3_out, pull_resistor_1_node, pull_resistor_2_node;
  wire [9:3] register_1_q_2;
  wire [9:8] undriven;

  Pull_Resistor pull_resistor_1 (.node(pull_resistor_1_node));
  assign pull_resistor_1_node = and_2_out ? pull_resistor_2_node : 10'bz;  // Controlled_Buffer controlled_buffer_1
  Demultiplexer #(.select(3), .width(10)) demultiplexer_1 (
    .out0(out_16), .out1(out_17), .out2(out_18), .out3(out_19), .out4(out_20), .out5(out_21), .out6(out_22),
    .out7(out_23), .in(pull_resistor_1_node), .sel(register_1_q));
  Multiplexer #(.select(3), .width(10)) multiplexer_1 (
    .in0(in_2), .in1(in_3), .in2(in_4), .in3(in_5), .in4(in_7), .in5(in_8), .in6(in_9), .in7(in_10),
    .out(multiplexer_1_out), .sel(register_1_q));
  Demultiplexer #(.select(3)) demultiplexer_2 (
    .out0(out_25), .out1(out_26), .out2(out_27), .out3(out_28), .out4(out_29), .out5(out_30), .out6(out_31),
    .out7(out_32), .in(register_1_q_2[4]), .sel(register_1_q));
  and and_1 (and_1_out, register_1_q_2[3], buffer_1_out);
  Demultiplexer #(.select(3)) demultiplexer_3 (
    .out0(out_33), .out1(out_34), .out2(out_35), .out3(out_36), .out4(out_37), .out5(out_38), .out6(out_39),
    .out7(out_40), .in(and_1_out), .sel(register_1_q));
  and and_2 (and_2_out, in_13, register_1_q_2[4]);
  Pull_Resistor pull_resistor_2 (.node(pull_resistor_2_node));
  Multiplexer #(.width(10)) multiplexer_2 (
    .in0(multiplexer_1_out), .in1(multiplexer_3_out), .out(pull_resistor_2_node), .sel(register_1_q_2[4]));
  Multiplexer #(.width(10)) multiplexer_3 (
    .in0(in_6), .in1({undriven, in_11[7:0]}), .out(multiplexer_3_out), .sel(in_11[8]));
  buf buffer_1 (buffer_1_out, buffer_2_out);
  buf buffer_2 (buffer_2_out, in_13);
  assign out_24 = in_1 ? pull_resistor_2_node : 10'bz;  // Controlled_Buffer controlled_buffer_2
  not not_1 (not_1_out, in_13);
  or or_1 (out_15, register_1_q_2[4], in_11[9]);
  Register #(.width(10)) register_1 (
    .D(in_12), .Q({register_1_q_2, register_1_q}), .clk(not_1_out), .clr(in_14));  // open: en
endmodule

module bit_splitter (
  input  [9:0] in_1,
  output out_2,
  output out_3,
  output out_4,
  output out_5,
  output out_6,
  output out_7,
  output out_8,
  output out_9,
  output out_10,
  output out_11
);

  wire [8:0] multiplier_9_out;
  wire [9:0] multiplier_1_out, multiplier_2_out, multiplier_3_out, multiplier_4_out, multiplier_5_out,
       multiplier_6_out, multiplier_7_out, multiplier_8_out;

  Multiplier #(.width(10)) multiplier_1 (.a(in_1), .b(10'h2), .out(multiplier_1_out));  // open: cin, cout
  Multiplier #(.width(10)) multiplier_2 (.a(multiplier_1_out), .b(10'h2), .out(multiplier_2_out));  // open: cin, cout
  Multiplier #(.width(10)) multiplier_3 (.a(multiplier_2_out), .b(10'h2), .out(multiplier_3_out));  // open: cin, cout
  Multiplier #(.width(10)) multiplier_4 (.a(multiplier_3_out), .b(10'h2), .out(multiplier_4_out));  // open: cin, cout
  Multiplier #(.width(10)) multiplier_5 (.a(multiplier_4_out), .b(10'h2), .out(multiplier_5_out));  // open: cin, cout
  Multiplier #(.width(10)) multiplier_6 (.a(multiplier_5_out), .b(10'h2), .out(multiplier_6_out));  // open: cin, cout
  Multiplier #(.width(10)) multiplier_7 (.a(multiplier_6_out), .b(10'h2), .out(multiplier_7_out));  // open: cin, cout
  Multiplier #(.width(10)) multiplier_8 (.a(multiplier_7_out), .b(10'h2), .out(multiplier_8_out));  // open: cin, cout
  Multiplier #(.width(10)) multiplier_9 (
    .a(multiplier_8_out), .b(10'h2), .out({out_11, multiplier_9_out}));  // open: cin, cout
  Comparator #(.mode("unsigned"), .width(10)) comparator_1 (.a(in_1), .b(10'h1ff), .gt(out_2));  // open: eq, lt
  Comparator #(.mode("unsigned"), .width(10)) comparator_2 (
    .a(multiplier_1_out), .b(10'h1ff), .gt(out_3));  // open: eq, lt
  Comparator #(.mode("unsigned"), .width(10)) comparator_3 (
    .a(multiplier_2_out), .b(10'h1ff), .gt(out_4));  // open: eq, lt
  Comparator #(.mode("unsigned"), .width(10)) comparator_4 (
    .a(multiplier_3_out), .b(10'h1ff), .gt(out_5));  // open: eq, lt
  Comparator #(.mode("unsigned"), .width(10)) comparator_5 (
    .a(multiplier_4_out), .b(10'h1ff), .gt(out_6));  // open: eq, lt
  Comparator #(.mode("unsigned"), .width(10)) comparator_6 (
    .a(multiplier_5_out), .b(10'h1ff), .gt(out_7));  // open: eq, lt
  Comparator #(.mode("unsigned"), .width(10)) comparator_7 (
    .a(multiplier_6_out), .b(10'h1ff), .gt(out_8));  // open: eq, lt
  Comparator #(.mode("unsigned"), .width(10)) comparator_8 (
    .a(multiplier_7_out), .b(10'h1ff), .gt(out_9));  // open: eq, lt
  Comparator #(.mode("unsigned"), .width(10)) comparator_9 (
    .a(multiplier_8_out), .b(10'h1ff), .gt(out_10));  // open: eq, lt
endmodule

module TTcpu_display (
  input  [9:0] in_1,
  input  [9:0] in_2,
  input  in_3,
  input  in_4,
  input  in_5
);

  wire and_1_out, bit_splitter_1_out_4, bit_splitter_1_out_5, bit_splitter_1_out_6, bit_splitter_1_out_7,
       bit_splitter_1_out_8, bit_splitter_1_out_9, bit_splitter_1_out_10, bit_splitter_1_out_11,
       bit_splitter_2_out_4, bit_splitter_2_out_5, bit_splitter_2_out_6, bit_splitter_2_out_7,
       bit_splitter_2_out_8, bit_splitter_2_out_9, bit_splitter_2_out_10, bit_splitter_2_out_11,
       bit_splitter_3_out_4, bit_splitter_3_out_5, bit_splitter_3_out_6, bit_splitter_3_out_7,
       bit_splitter_3_out_8, bit_splitter_3_out_9, bit_splitter_3_out_10, bit_splitter_3_out_11,
       bit_splitter_4_out_4, bit_splitter_4_out_5, bit_splitter_4_out_6, bit_splitter_4_out_7,
       bit_splitter_4_out_8, bit_splitter_4_out_9, bit_splitter_4_out_10, bit_splitter_4_out_11,
       bit_splitter_5_out_4, bit_splitter_5_out_5, bit_splitter_5_out_6, bit_splitter_5_out_7,
       bit_splitter_5_out_8, bit_splitter_5_out_9, bit_splitter_5_out_10, bit_splitter_5_out_11,
       bit_splitter_6_out_4, bit_splitter_6_out_5, bit_splitter_6_out_6, bit_splitter_6_out_7,
       bit_splitter_6_out_8, bit_splitter_6_out_9, bit_splitter_6_out_10, bit_splitter_6_out_11,
       bit_splitter_7_out_4, bit_splitter_7_out_5, bit_splitter_7_out_6, bit_splitter_7_out_7,
       bit_splitter_7_out_8, bit_splitter_7_out_9, bit_splitter_7_out_10, bit_splitter_7_out_11,
       bit_splitter_8_out_4, bit_splitter_8_out_5, bit_splitter_8_out_6, bit_splitter_8_out_7,
       bit_splitter_8_out_8, bit_splitter_8_out_9, bit_splitter_8_out_10, bit_splitter_8_out_11,
       bit_splitter_9_out_4, bit_splitter_9_out_5, bit_splitter_9_out_6, bit_splitter_9_out_7,
       bit_splitter_9_out_8, bit_splitter_9_out_9, bit_splitter_9_out_10, bit_splitter_9_out_11,
       bit_splitter_10_out_4, bit_splitter_10_out_5, bit_splitter_10_out_6, bit_splitter_10_out_7,
       bit_splitter_10_out_8, bit_splitter_10_out_9, bit_splitter_10_out_10, bit_splitter_10_out_11,
       bit_splitter_11_out_4, bit_splitter_11_out_5, bit_splitter_11_out_6, bit_splitter_11_out_7,
       bit_splitter_11_out_8, bit_splitter_11_out_9, bit_splitter_11_out_10, bit_splitter_11_out_11,
       bit_splitter_12_out_4, bit_splitter_12_out_5, bit_splitter_12_out_6, bit_splitter_12_out_7,
       bit_splitter_12_out_8, bit_splitter_12_out_9, bit_splitter_12_out_10, bit_splitter_12_out_11,
       bit_splitter_13_out_4, bit_splitter_13_out_5, bit_splitter_13_out_6, bit_splitter_13_out_7,
       bit_splitter_13_out_8, bit_splitter_13_out_9, bit_splitter_13_out_10, bit_splitter_13_out_11,
       bit_splitter_14_out_4, bit_splitter_14_out_5, bit_splitter_14_out_6, bit_splitter_14_out_7,
       bit_splitter_14_out_8, bit_splitter_14_out_9, bit_splitter_14_out_10, bit_splitter_14_out_11,
       bit_splitter_15_out_4, bit_splitter_15_out_5, bit_splitter_15_out_6, bit_splitter_15_out_7,
       bit_splitter_15_out_8, bit_splitter_15_out_9, bit_splitter_15_out_10, bit_splitter_15_out_11,
       bit_splitter_16_out_4, bit_splitter_16_out_5, bit_splitter_16_out_6, bit_splitter_16_out_7,
       bit_splitter_16_out_8, bit_splitter_16_out_9, bit_splitter_16_out_10, bit_splitter_16_out_11,
       bit_splitter_17_out_4, bit_splitter_17_out_5, bit_splitter_17_out_6, bit_splitter_17_out_7,
       bit_splitter_17_out_8, bit_splitter_17_out_9, bit_splitter_17_out_10, bit_splitter_17_out_11,
       bit_splitter_18_out_4, bit_splitter_18_out_5, bit_splitter_18_out_6, bit_splitter_18_out_7,
       bit_splitter_18_out_8, bit_splitter_18_out_9, bit_splitter_18_out_10, bit_splitter_18_out_11,
       buffer_1_out, buffer_2_out, buffer_3_out, demultiplexer_2_out0, demultiplexer_2_out1,
       demultiplexer_2_out2, demultiplexer_2_out3, demultiplexer_2_out4, demultiplexer_2_out5,
       demultiplexer_2_out6, demultiplexer_2_out7, demultiplexer_2_out8, demultiplexer_2_out9,
       demultiplexer_2_out10, demultiplexer_2_out11, demultiplexer_2_out12, demultiplexer_2_out13,
       demultiplexer_2_out14, demultiplexer_2_out15, demultiplexer_2_out16, demultiplexer_2_out17,
       j_k_ff_1_q, j_k_ff_1_qn, not_1_out;
  wire [4:0] register_1_q;
  wire [7:0] register_2_q, register_3_q, register_4_q, register_5_q, register_6_q, register_7_q,
       register_8_q, register_9_q, register_10_q, register_11_q, register_12_q, register_13_q, register_14_q,
       register_15_q, register_16_q, register_17_q, register_18_q, register_19_q;
  wire [9:0] demultiplexer_1_out0, demultiplexer_1_out1;
  wire [9:8] undriven, undriven_2, undriven_3, undriven_4, undriven_5, undriven_6, undriven_7, undriven_8,
       undriven_9, undriven_10, undriven_11, undriven_12, undriven_13, undriven_14, undriven_15, undriven_16,
       undriven_17, undriven_18;

  and and_1 (and_1_out, j_k_ff_1_q, in_3);
  Demultiplexer #(.width(10)) demultiplexer_1 (
    .out0(demultiplexer_1_out0), .out1(demultiplexer_1_out1), .in(in_1), .sel(j_k_ff_1_qn));
  J_K_Flip_Flop j_k_ff_1 (
    .J(not_1_out), .clk(not_1_out), .K(not_1_out), .Q(j_k_ff_1_q), .Qn(j_k_ff_1_qn), .reset(in_5));  // open: preset
  not not_1 (not_1_out, in_4);
  Demultiplexer #(.select(5)) demultiplexer_2 (
    .out0(demultiplexer_2_out0), .out1(demultiplexer_2_out1), .out2(demultiplexer_2_out2),
    .out3(demultiplexer_2_out3), .out4(demultiplexer_2_out4), .out5(demultiplexer_2_out5),
    .out6(demultiplexer_2_out6), .out7(demultiplexer_2_out7), .out8(demultiplexer_2_out8),
    .out9(demultiplexer_2_out9), .out10(demultiplexer_2_out10), .out11(demultiplexer_2_out11),
    .out12(demultiplexer_2_out12), .out13(demultiplexer_2_out13), .out14(demultiplexer_2_out14),
    .out15(demultiplexer_2_out15), .out16(demultiplexer_2_out16), .out17(demultiplexer_2_out17),
    .in(and_1_out), .sel(register_1_q));  // open: out18, out19, out20, out21, out22, out23, out24, out25, out26, out27, out28, out29, out30, out31
  Register #(.width(5)) register_1 (
    .D(demultiplexer_1_out1[4:0]), .en(j_k_ff_1_qn), .Q(register_1_q), .clk(buffer_3_out), .clr(in_5));
  buf buffer_1 (buffer_1_out, in_4);
  buf buffer_2 (buffer_2_out, buffer_1_out);
  buf buffer_3 (buffer_3_out, buffer_2_out);
  Register register_2 (
    .D(demultiplexer_1_out0[7:0]), .en(demultiplexer_2_out0), .Q(register_2_q), .clk(buffer_3_out), .clr(in_5));
  Register register_3 (
    .D(demultiplexer_1_out0[7:0]), .en(demultiplexer_2_out2), .Q(register_3_q), .clk(buffer_3_out), .clr(in_5));
  Register register_4 (
    .D(demultiplexer_1_out0[7:0]), .en(demultiplexer_2_out4), .Q(register_4_q), .clk(buffer_3_out), .clr(in_5));
  Register register_5 (
    .D(demultiplexer_1_out0[7:0]), .en(demultiplexer_2_out6), .Q(register_5_q), .clk(buffer_3_out), .clr(in_5));
  Register register_6 (
    .D(demultiplexer_1_out0[7:0]), .en(demultiplexer_2_out8), .Q(register_6_q), .clk(buffer_3_out), .clr(in_5));
  Register register_7 (
    .D(demultiplexer_1_out0[7:0]), .en(demultiplexer_2_out10), .Q(register_7_q), .clk(buffer_3_out),
    .clr(in_5));
  Register register_8 (
    .D(demultiplexer_1_out0[7:0]), .en(demultiplexer_2_out12), .Q(register_8_q), .clk(buffer_3_out),
    .clr(in_5));
  Register register_9 (
    .D(demultiplexer_1_out0[7:0]), .en(demultiplexer_2_out14), .Q(register_9_q), .clk(buffer_3_out),
    .clr(in_5));
  Register register_10 (
    .D(demultiplexer_1_out0[7:0]), .en(demultiplexer_2_out16), .Q(register_10_q), .clk(buffer_3_out),
    .clr(in_5));
  LED led_1 (.in(bit_splitter_1_out_4));
  LED led_2 (.in(bit_splitter_1_out_5));
  bit_splitter bit_splitter_1 (
    .in_1({undriven, register_2_q}), .out_4(bit_splitter_1_out_4), .out_5(bit_splitter_1_out_5),
    .out_6(bit_splitter_1_out_6), .out_7(bit_splitter_1_out_7), .out_8(bit_splitter_1_out_8),
    .out_9(bit_splitter_1_out_9), .out_10(bit_splitter_1_out_10), .out_11(bit_splitter_1_out_11));  // open: out_2, out_3
  LED led_3 (.in(bit_splitter_2_out_4));
  LED led_4 (.in(bit_splitter_2_out_5));
  bit_splitter bit_splitter_2 (
    .in_1({undriven_2, register_3_q}), .out_4(bit_splitter_2_out_4), .out_5(bit_splitter_2_out_5),
    .out_6(bit_splitter_2_out_6), .out_7(bit_splitter_2_out_7), .out_8(bit_splitter_2_out_8),
    .out_9(bit_splitter_2_out_9), .out_10(bit_splitter_2_out_10), .out_11(bit_splitter_2_out_11));  // open: out_2, out_3
  LED led_5 (.in(bit_splitter_3_out_4));
  LED led_6 (.in(bit_splitter_3_out_5));
  bit_splitter bit_splitter_3 (
    .in_1({undriven_3, register_4_q}), .out_4(bit_splitter_3_out_4), .out_5(bit_splitter_3_out_5),
    .out_6(bit_splitter_3_out_6), .out_7(bit_splitter_3_out_7), .out_8(bit_splitter_3_out_8),
    .out_9(bit_splitter_3_out_9), .out_10(bit_splitter_3_out_10), .out_11(bit_splitter_3_out_11));  // open: out_2, out_3
  LED led_7 (.in(bit_splitter_4_out_4));
  LED led_8 (.in(bit_splitter_4_out_5));
  bit_splitter bit_splitter_4 (
    .in_1({undriven_4, register_5_q}), .out_4(bit_splitter_4_out_4), .out_5(bit_splitter_4_out_5),
    .out_6(bit_splitter_4_out_6), .out_7(bit_splitter_4_out_7), .out_8(bit_splitter_4_out_8),
    .out_9(bit_splitter_4_out_9), .out_10(bit_splitter_4_out_10), .out_11(bit_splitter_4_out_11));  // open: out_2, out_3
  LED led_9 (.in(bit_splitter_5_out_4));
  LED led_10 (.in(bit_splitter_5_out_5));
  bit_splitter bit_splitter_5 (
    .in_1({undriven_5, register_6_q}), .out_4(bit_splitter_5_out_4), .out_5(bit_splitter_5_out_5),
    .out_6(bit_splitter_5_out_6), .out_7(bit_splitter_5_out_7), .out_8(bit_splitter_5_out_8),
    .out_9(bit_splitter_5_out_9), .out_10(bit_splitter_5_out_10), .out_11(bit_splitter_5_out_11));  // open: out_2, out_3
  LED led_11 (.in(bit_splitter_6_out_4));
  LED led_12 (.in(bit_splitter_6_out_5));
  bit_splitter bit_splitter_6 (
    .in_1({undriven_6, register_7_q}), .out_4(bit_splitter_6_out_4), .out_5(bit_splitter_6_out_5),
    .out_6(bit_splitter_6_out_6), .out_7(bit_splitter_6_out_7), .out_8(bit_splitter_6_out_8),
    .out_9(bit_splitter_6_out_9), .out_10(bit_splitter_6_out_10), .out_11(bit_splitter_6_out_11));  // open: out_2, out_3
  LED led_13 (.in(bit_splitter_7_out_4));
  LED led_14 (.in(bit_splitter_7_out_5));
  bit_splitter bit_splitter_7 (
    .in_1({undriven_7, register_8_q}), .out_4(bit_splitter_7_out_4), .out_5(bit_splitter_7_out_5),
    .out_6(bit_splitter_7_out_6), .out_7(bit_splitter_7_out_7), .out_8(bit_splitter_7_out_8),
    .out_9(bit_splitter_7_out_9), .out_10(bit_splitter_7_out_10), .out_11(bit_splitter_7_out_11));  // open: out_2, out_3
  LED led_15 (.in(bit_splitter_8_out_4));
  LED led_16 (.in(bit_splitter_8_out_5));
  bit_splitter bit_splitter_8 (
    .in_1({undriven_8, register_9_q}), .out_4(bit_splitter_8_out_4), .out_5(bit_splitter_8_out_5),
    .out_6(bit_splitter_8_out_6), .out_7(bit_splitter_8_out_7), .out_8(bit_splitter_8_out_8),
    .out_9(bit_splitter_8_out_9), .out_10(bit_splitter_8_out_10), .out_11(bit_splitter_8_out_11));  // open: out_2, out_3
  LED led_17 (.in(bit_splitter_9_out_4));
  LED led_18 (.in(bit_splitter_9_out_5));
  bit_splitter bit_splitter_9 (
    .in_1({undriven_9, register_10_q}), .out_4(bit_splitter_9_out_4), .out_5(bit_splitter_9_out_5),
    .out_6(bit_splitter_9_out_6), .out_7(bit_splitter_9_out_7), .out_8(bit_splitter_9_out_8),
    .out_9(bit_splitter_9_out_9), .out_10(bit_splitter_9_out_10), .out_11(bit_splitter_9_out_11));  // open: out_2, out_3
  LED led_19 (.in(bit_splitter_1_out_6));
  LED led_20 (.in(bit_splitter_1_out_7));
  LED led_21 (.in(bit_splitter_1_out_8));
  LED led_22 (.in(bit_splitter_1_out_9));
  LED led_23 (.in(bit_splitter_2_out_6));
  LED led_24 (.in(bit_splitter_2_out_7));
  LED led_25 (.in(bit_splitter_2_out_8));
  LED led_26 (.in(bit_splitter_2_out_9));
  LED led_27 (.in(bit_splitter_3_out_6));
  LED led_28 (.in(bit_splitter_3_out_7));
  LED led_29 (.in(bit_splitter_3_out_8));
  LED led_30 (.in(bit_splitter_3_out_9));
  LED led_31 (.in(bit_splitter_4_out_6));
  LED led_32 (.in(bit_splitter_4_out_7));
  LED led_33 (.in(bit_splitter_4_out_8));
  LED led_34 (.in(bit_splitter_4_out_9));
  LED led_35 (.in(bit_splitter_5_out_6));
  LED led_36 (.in(bit_splitter_5_out_7));
  LED led_37 (.in(bit_splitter_5_out_8));
  LED led_38 (.in(bit_splitter_5_out_9));
  LED led_39 (.in(bit_splitter_6_out_6));
  LED led_40 (.in(bit_splitter_6_out_7));
  LED led_41 (.in(bit_splitter_6_out_8));
  LED led_42 (.in(bit_splitter_6_out_9));
  LED led_43 (.in(bit_splitter_7_out_6));
  LED led_44 (.in(bit_splitter_7_out_7));
  LED led_45 (.in(bit_splitter_7_out_8));
  LED led_46 (.in(bit_splitter_7_out_9));
  LED led_47 (.in(bit_splitter_8_out_6));
  LED led_48 (.in(bit_splitter_8_out_7));
  LED led_49 (.in(bit_splitter_8_out_8));
  LED led_50 (.in(bit_splitter_8_out_9));
  LED led_51 (.in(bit_splitter_9_out_6));
  LED led_52 (.in(bit_splitter_9_out_7));
  LED led_53 (.in(bit_splitter_9_out_8));
  LED led_54 (.in(bit_splitter_9_out_9));
  LED led_55 (.in(bit_splitter_1_out_10));
  LED led_56 (.in(bit_splitter_1_out_11));
  LED led_57 (.in(bit_splitter_2_out_10));
  LED led_58 (.in(bit_splitter_2_out_11));
  LED led_59 (.in(bit_splitter_3_out_10));
  LED led_60 (.in(bit_splitter_3_out_11));
  LED led_61 (.in(bit_splitter_4_out_10));
  LED led_62 (.in(bit_splitter_4_out_11));
  LED led_63 (.in(bit_splitter_5_out_10));
  LED led_64 (.in(bit_splitter_5_out_11));
  LED led_65 (.in(bit_splitter_6_out_10));
  LED led_66 (.in(bit_splitter_6_out_11));
  LED led_67 (.in(bit_splitter_7_out_10));
  LED led_68 (.in(bit_splitter_7_out_11));
  LED led_69 (.in(bit_splitter_8_out_10));
  LED led_70 (.in(bit_splitter_8_out_11));
  LED led_71 (.in(bit_splitter_9_out_10));
  LED led_72 (.in(bit_splitter_9_out_11));
  bit_splitter bit_splitter_10 (
    .in_1({undriven_10, register_11_q}), .out_4(bit_splitter_10_out_4), .out_5(bit_splitter_10_out_5),
    .out_6(bit_splitter_10_out_6), .out_7(bit_splitter_10_out_7), .out_8(bit_splitter_10_out_8),
    .out_9(bit_splitter_10_out_9), .out_10(bit_splitter_10_out_10), .out_11(bit_splitter_10_out_11));  // open: out_2, out_3
  Register register_11 (
    .D(demultiplexer_1_out0[7:0]), .en(demultiplexer_2_out1), .Q(register_11_q), .clk(buffer_3_out),
    .clr(in_5));
  bit_splitter bit_splitter_11 (
    .in_1({undriven_11, register_12_q}), .out_4(bit_splitter_11_out_4), .out_5(bit_splitter_11_out_5),
    .out_6(bit_splitter_11_out_6), .out_7(bit_splitter_11_out_7), .out_8(bit_splitter_11_out_8),
    .out_9(bit_splitter_11_out_9), .out_10(bit_splitter_11_out_10), .out_11(bit_splitter_11_out_11));  // open: out_2, out_3
  Register register_12 (
    .D(demultiplexer_1_out0[7:0]), .en(demultiplexer_2_out3), .Q(register_12_q), .clk(buffer_3_out),
    .clr(in_5));
  bit_splitter bit_splitter_12 (
    .in_1({undriven_12, register_13_q}), .out_4(bit_splitter_12_out_4), .out_5(bit_splitter_12_out_5),
    .out_6(bit_splitter_12_out_6), .out_7(bit_splitter_12_out_7), .out_8(bit_splitter_12_out_8),
    .out_9(bit_splitter_12_out_9), .out_10(bit_splitter_12_out_10), .out_11(bit_splitter_12_out_11));  // open: out_2, out_3
  Register register_13 (
    .D(demultiplexer_1_out0[7:0]), .en(demultiplexer_2_out5), .Q(register_13_q), .clk(buffer_3_out),
    .clr(in_5));
  bit_splitter bit_splitter_13 (
    .in_1({undriven_13, register_14_q}), .out_4(bit_splitter_13_out_4), .out_5(bit_splitter_13_out_5),
    .out_6(bit_splitter_13_out_6), .out_7(bit_splitter_13_out_7), .out_8(bit_splitter_13_out_8),
    .out_9(bit_splitter_13_out_9), .out_10(bit_splitter_13_out_10), .out_11(bit_splitter_13_out_11));  // open: out_2, out_3
  Register register_14 (
    .D(demultiplexer_1_out0[7:0]), .en(demultiplexer_2_out7), .Q(register_14_q), .clk(buffer_3_out),
    .clr(in_5));
  bit_splitter bit_splitter_14 (
    .in_1({undriven_14, register_15_q}), .out_4(bit_splitter_14_out_4), .out_5(bit_splitter_14_out_5),
    .out_6(bit_splitter_14_out_6), .out_7(bit_splitter_14_out_7), .out_8(bit_splitter_14_out_8),
    .out_9(bit_splitter_14_out_9), .out_10(bit_splitter_14_out_10), .out_11(bit_splitter_14_out_11));  // open: out_2, out_3
  Register register_15 (
    .D(demultiplexer_1_out0[7:0]), .en(demultiplexer_2_out9), .Q(register_15_q), .clk(buffer_3_out),
    .clr(in_5));
  bit_splitter bit_splitter_15 (
    .in_1({undriven_15, register_16_q}), .out_4(bit_splitter_15_out_4), .out_5(bit_splitter_15_out_5),
    .out_6(bit_splitter_15_out_6), .out_7(bit_splitter_15_out_7), .out_8(bit_splitter_15_out_8),
    .out_9(bit_splitter_15_out_9), .out_10(bit_splitter_15_out_10), .out_11(bit_splitter_15_out_11));  // open: out_2, out_3
  Register register_16 (
    .D(demultiplexer_1_out0[7:0]), .en(demultiplexer_2_out11), .Q(register_16_q), .clk(buffer_3_out),
    .clr(in_5));
  bit_splitter bit_splitter_16 (
    .in_1({undriven_16, register_17_q}), .out_4(bit_splitter_16_out_4), .out_5(bit_splitter_16_out_5),
    .out_6(bit_splitter_16_out_6), .out_7(bit_splitter_16_out_7), .out_8(bit_splitter_16_out_8),
    .out_9(bit_splitter_16_out_9), .out_10(bit_splitter_16_out_10), .out_11(bit_splitter_16_out_11));  // open: out_2, out_3
  Register register_17 (
    .D(demultiplexer_1_out0[7:0]), .en(demultiplexer_2_out13), .Q(register_17_q), .clk(buffer_3_out),
    .clr(in_5));
  bit_splitter bit_splitter_17 (
    .in_1({undriven_17, register_18_q}), .out_4(bit_splitter_17_out_4), .out_5(bit_splitter_17_out_5),
    .out_6(bit_splitter_17_out_6), .out_7(bit_splitter_17_out_7), .out_8(bit_splitter_17_out_8),
    .out_9(bit_splitter_17_out_9), .out_10(bit_splitter_17_out_10), .out_11(bit_splitter_17_out_11));  // open: out_2, out_3
  Register register_18 (
    .D(demultiplexer_1_out0[7:0]), .en(demultiplexer_2_out15), .Q(register_18_q), .clk(buffer_3_out),
    .clr(in_5));
  bit_splitter bit_splitter_18 (
    .in_1({undriven_18, register_19_q}), .out_4(bit_splitter_18_out_4), .out_5(bit_splitter_18_out_5),
    .out_6(bit_splitter_18_out_6), .out_7(bit_splitter_18_out_7), .out_8(bit_splitter_18_out_8),
    .out_9(bit_splitter_18_out_9), .out_10(bit_splitter_18_out_10), .out_11(bit_splitter_18_out_11));  // open: out_2, out_3
  Register register_19 (
    .D(demultiplexer_1_out0[7:0]), .en(demultiplexer_2_out17), .Q(register_19_q), .clk(buffer_3_out),
    .clr(in_5));
  LED led_73 (.in(bit_splitter_10_out_4));
  LED led_74 (.in(bit_splitter_10_out_5));
  LED led_75 (.in(bit_splitter_10_out_6));
  LED led_76 (.in(bit_splitter_10_out_7));
  LED led_77 (.in(bit_splitter_11_out_4));
  LED led_78 (.in(bit_splitter_11_out_5));
  LED led_79 (.in(bit_splitter_11_out_6));
  LED led_80 (.in(bit_splitter_11_out_7));
  LED led_81 (.in(bit_splitter_12_out_4));
  LED led_82 (.in(bit_splitter_12_out_5));
  LED led_83 (.in(bit_splitter_12_out_6));
  LED led_84 (.in(bit_splitter_12_out_7));
  LED led_85 (.in(bit_splitter_13_out_4));
  LED led_86 (.in(bit_splitter_13_out_5));
  LED led_87 (.in(bit_splitter_13_out_6));
  LED led_88 (.in(bit_splitter_13_out_7));
  LED led_89 (.in(bit_splitter_14_out_4));
  LED led_90 (.in(bit_splitter_14_out_5));
  LED led_91 (.in(bit_splitter_14_out_6));
  LED led_92 (.in(bit_splitter_14_out_7));
  LED led_93 (.in(bit_splitter_15_out_4));
  LED led_94 (.in(bit_splitter_15_out_5));
  LED led_95 (.in(bit_splitter_15_out_6));
  LED led_96 (.in(bit_splitter_15_out_7));
  LED led_97 (.in(bit_splitter_16_out_4));
  LED led_98 (.in(bit_splitter_16_out_5));
  LED led_99 (.in(bit_splitter_16_out_6));
  LED led_100 (.in(bit_splitter_16_out_7));
  LED led_101 (.in(bit_splitter_17_out_4));
  LED led_102 (.in(bit_splitter_17_out_5));
  LED led_103 (.in(bit_splitter_17_out_6));
  LED led_104 (.in(bit_splitter_17_out_7));
  LED led_105 (.in(bit_splitter_18_out_4));
  LED led_106 (.in(bit_splitter_18_out_5));
  LED led_107 (.in(bit_splitter_18_out_6));
  LED led_108 (.in(bit_splitter_18_out_7));
  LED led_109 (.in(bit_splitter_10_out_8));
  LED led_110 (.in(bit_splitter_10_out_9));
  LED led_111 (.in(bit_splitter_10_out_10));
  LED led_112 (.in(bit_splitter_10_out_11));
  LED led_113 (.in(bit_splitter_11_out_8));
  LED led_114 (.in(bit_splitter_11_out_9));
  LED led_115 (.in(bit_splitter_11_out_10));
  LED led_116 (.in(bit_splitter_11_out_11));
  LED led_117 (.in(bit_splitter_12_out_8));
  LED led_118 (.in(bit_splitter_12_out_9));
  LED led_119 (.in(bit_splitter_12_out_10));
  LED led_120 (.in(bit_splitter_12_out_11));
  LED led_121 (.in(bit_splitter_13_out_8));
  LED led_122 (.in(bit_splitter_13_out_9));
  LED led_123 (.in(bit_splitter_13_out_10));
  LED led_124 (.in(bit_splitter_13_out_11));
  LED led_125 (.in(bit_splitter_14_out_8));
  LED led_126 (.in(bit_splitter_14_out_9));
  LED led_127 (.in(bit_splitter_14_out_10));
  LED led_128 (.in(bit_splitter_14_out_11));
  LED led_129 (.in(bit_splitter_15_out_8));
  LED led_130 (.in(bit_splitter_15_out_9));
  LED led_131 (.in(bit_splitter_15_out_10));
  LED led_132 (.in(bit_splitter_15_out_11));
  LED led_133 (.in(bit_splitter_16_out_8));
  LED led_134 (.in(bit_splitter_16_out_9));
  LED led_135 (.in(bit_splitter_16_out_10));
  LED led_136 (.in(bit_splitter_16_out_11));
  LED led_137 (.in(bit_splitter_17_out_8));
  LED led_138 (.in(bit_splitter_17_out_9));
  LED led_139 (.in(bit_splitter_17_out_10));
  LED led_140 (.in(bit_splitter_17_out_11));
  LED led_141 (.in(bit_splitter_18_out_8));
  LED led_142 (.in(bit_splitter_18_out_9));
  LED led_143 (.in(bit_splitter_18_out_10));
  LED led_144 (.in(bit_splitter_18_out_11));
endmodule

module TTcpu_7seg (
  input  [9:0] in_1,
  input  in_2,
  input  in_3,
  input  in_4,
  output [9:0] out_5
);

  Hex_Digit_Display hex_digit_display_1 ();  // open: value, dp
  Register #(.width(10)) register_1 (.D(in_1), .en(in_2), .clk(in_3), .clr(in_4));  // open: Q
  // Binary_to_BCD_converter #(.binvalue(10)) binary_to_bcd_converter_1: pin names not known
  Hex_Digit_Display hex_digit_display_2 ();  // open: value, dp
  Hex_Digit_Display hex_digit_display_3 ();  // open: value, dp
  Hex_Digit_Display hex_digit_display_4 ();  // open: value, dp

  assign out_5 = {10{1'b0}};
endmodule

module TTcpu_inputator (
  input  [9:0] in_1,
  input  [9:0] in_2,
  input  in_3,
  input  in_4,
  input  in_5,
  input  in_6,
  output out_7,
  output [9:0] out_8
);

  wire and_1_out, and_2_out, or_1_out;
  wire [9:0] j_k_ff_1_q;

  and and_1 (and_1_out, ~in_3, in_4);  // AND_Gate
  J_K_Flip_Flop j_k_ff_1 (.J(in_5), .clk(in_5), .K(in_5), .Q(j_k_ff_1_q[0]), .reset(or_1_out));  // open: Qn, preset
  or or_1 (or_1_out, and_1_out, in_6);
  and and_2 (and_2_out, in_3, in_4);
  D_Flip_Flop d_ff_1 (.clk(and_2_out), .D(in_2[0]), .Q(out_7), .reset(in_6));  // open: Qn, preset
  Multiplexer #(.width(10)) multiplexer_1 (.in0(in_1), .in1(j_k_ff_1_q), .out(out_8), .sel(out_7));
endmodule
